# Fritzing sketch ardubot-control (saved by Fritzing 0.9.3b)

parts:
  U1 = LIPO-110mAh [package=lipo-110]
  Part4 = NRF24L01+ Breakout Board
  Part5 = Thumb Joystick
  Part6 = Arduino Pro Mini 328 - 3.3 V/8MHz

nets:
  VCC: U1.+, Part4.VCC, Part5.VCC, Part6.VCC
  GND: U1.-, Part5.GND, Part6.GND#26, Part6.GND#45
  N1: Part4.GND, Part6.GND#51
  N2: Part4.CE, Part6.D9_PWM
  N3: Part4.CS, Part6.D10_PWM/SS
  N4: Part4.SCK, Part6.D13/SCK
  N5: Part4.MOSI, Part6.D11_PWM/MOSI
  N6: Part4.MISO, Part6.D12/MISO
  N7: Part5.SEL, Part6.D3_PWM
  N8: Part5.HORZ, Part6.A2
  N9: Part5.VERT, Part6.A3

notes:
  NRF24L01
  BRUSHLESS 23mm

custom parts:
  Arduino Pro Mini 328 - 3.3 V/8MHz: Versión de Arduino Pro Mini basada en MEGA328P a 8MHz y alimentada a 3.3 voltios.
