# Fritzing sketch ardubot (saved by Fritzing 0.9.3b)

parts:
  U1 = LIPO-110mAh [package=lipo-110]
  Part4 = NRF24L01+ Breakout Board
  U2 = LIPO-110mAh [package=lipo-110]
  Part6 = Arduino Pro Mini 328 - 3.3 V/8MHz
  U6 = Motor
  U5 = Motor
  ESC2 = ESC 10A 2s
  Brushless_23mm1 = Brushless Motor 23mm
  H1 = H Bridge

nets:
  N1: U1.+, Part6.RAW, H1.VCC
  GND: U1.-, Part4.GND, Part6.GND#26, H1.GND
  VCC: Part4.VCC, Part6.VCC
  N2: Part4.CE, Part6.D9_PWM
  N3: Part4.CS, Part6.D10_PWM/SS
  N4: Part4.SCK, Part6.D13/SCK
  N5: Part4.MOSI, Part6.D11_PWM/MOSI
  N6: Part4.MISO, Part6.D12/MISO
  N7: U2.+, ESC2.+12V
  N8: U2.-, ESC2.GROUND
  N9: Part6.D7, ESC2.DATA
  N10: Part6.D6_PWM, H1.A-1B
  N11: Part6.D5_PWM, H1.A-1A
  N12: Part6.D4, H1.B-1B
  N13: Part6.D3_PWM, H1.B-1A
  N14: Part6.GND#51, ESC2.GND
  N15: U6.PIN_1, H1.A_Pin_2
  N16: U6.PIN_2, H1.A_Pin_1
  N17: U5.PIN_1, H1.B_Pin_2
  N18: U5.PIN_2, H1.B_Pin_1
  N19: ESC2.U, Brushless_23mm1.u
  N20: ESC2.V, Brushless_23mm1.v
  N21: ESC2.W, Brushless_23mm1.w

notes:
  L9110S
  NRF24L01
  ESC 10A 2s
  BRUSHLESS 23mm

custom parts:
  Arduino Pro Mini 328 - 3.3 V/8MHz: Versión de Arduino Pro Mini basada en MEGA328P a 8MHz y alimentada a 3.3 voltios.
  Motor: Micro Motor
  Brushless Motor 23mm: Brushless Outrunner Motor 23mm
  H Bridge: H Bridge brushed motor driver
