# Fritzing sketch compost temp (saved by Fritzing 0.9.3b)

parts:
  U1 = ESP8266 WiFi Module [part_number=ESP8266]
  Part1 = Arduino Pro Mini 328 - 3.3 V/8MHz
  BAT1 = Battery Holders [package=battcom_20mm_pth]
  DS1 = DS18B20 1-Wire Temperature Sensor [part_number=DS18B20]
  R1 = Resistor [tolerance=±5% resistance=4.7k package=THT]

nets:
  VCC: U1.VCC, Part1.VCC, DS1.VDD, R1.Pin_0
  GND: U1.GND, Part1.GND, BAT1.-, DS1.GND
  N1: Part1.RAW, BAT1.+
  N2: Part1.D2, DS1.DQ, R1.Pin_1

custom parts:
  Arduino Pro Mini 328 - 3.3 V/8MHz: Versión de Arduino Pro Mini basada en MEGA328P a 8MHz y alimentada a 3.3 voltios.
